# Fritzing sketch SolarTracker_schema (saved by Fritzing 0.9.3b)
breadboards: 1
perfboards: 1

parts:
  M1 = BMP280
  Componente2 = MicroSD Card Module
  J1 = Basic Servo
  J2 = Basic Servo
  U1 = LCD-16X2 [package=lcd-16x2]
  PCB2 = RTC_DS1302_module
  LCM1602_IIC1 = LCM1602 IIC [part_number="LCM1602 IIC" chip_label="LCM1602 IIC" package="DIP (Dual Inline) [THT]"]
  Water_Level_Sensor1 = Water Level Sensor
  R1 = PHOTOCELL [package=photocell]
  R2 = PHOTOCELL [package=photocell]
  R3 = PHOTOCELL [package=photocell]
  R4 = PHOTOCELL [package=photocell]
  R5 = Resistor [tolerance=±5% resistance=10k package=THT]
  R6 = Resistor [tolerance=±5% resistance=10k package=THT]
  R7 = Resistor [tolerance=±5% resistance=10k package=THT]
  R8 = Resistor [tolerance=±5% resistance=10k package=THT]
  Componente1 = Arduino Yun
  VCC1 = 4 x AAA Battery Mount

nets:
  VIN: M1.VIN, Componente1.3V3
  GND: M1.GND, Componente2.GND, PCB2.GND, LCM1602_IIC1.GND, Water_Level_Sensor1.GND, R1.P$1, R2.P$1, R3.P$2, R4.P$1, Componente1.GND
  N1: M1.SCL, LCM1602_IIC1.SCL, Componente1.A5/SCL
  N2: M1.SDA, LCM1602_IIC1.SDA, Componente1.A4/SDA
  VCC: Componente2.VCC, PCB2.VCC, LCM1602_IIC1.VCC, Water_Level_Sensor1.VCC, R5.Pin_0, R6.Pin_0, R7.Pin_0, R8.Pin_0, Componente1.5V
  N3: Componente2.MISO, Componente1.D12/MISO
  N4: Componente2.MOSI, Componente1.D11_PWM/MOSI
  N5: Componente2.SCK, Componente1.D13/SCK
  N6: Componente2.CS, Componente1.D10_PWM/SS
  GND_2: J1.gnd, J2.gnd, VCC1.-
  VCC_2: J1.vcc, J2.vcc, VCC1.+
  N7: J1.pulse, Componente1.D5_PWM
  N8: J2.pulse, Componente1.D6_PWM
  VSS: U1.VSS, LCM1602_IIC1.VSS
  VDD: U1.VDD, LCM1602_IIC1.VDD
  N9: U1.VO, LCM1602_IIC1.V0
  N10: U1.RS, LCM1602_IIC1.RS
  N11: U1.R_W, LCM1602_IIC1.RW
  N12: U1.E, LCM1602_IIC1.E
  N13: U1.DB0, LCM1602_IIC1.D0
  N14: U1.DB1, LCM1602_IIC1.D1
  N15: U1.DB2, LCM1602_IIC1.D2
  N16: U1.DB3, LCM1602_IIC1.D3
  N17: U1.DB4, LCM1602_IIC1.D4
  N18: U1.DB5, LCM1602_IIC1.D5
  N19: U1.DB6, LCM1602_IIC1.D6
  N20: U1.DB7, LCM1602_IIC1.D7
  N21: U1.A, LCM1602_IIC1.A
  N22: U1.K, LCM1602_IIC1.K
  N23: PCB2.RST, Componente1.D7
  N24: PCB2.DAT, Componente1.D4
  N25: PCB2.CLK, Componente1.D3_PWM
  N26: Water_Level_Sensor1.SIG, Componente1.D8
  N27: R1.P$2, R7.Pin_1, Componente1.A2
  N28: R2.P$2, R8.Pin_1, Componente1.A0
  N29: R3.P$1, R5.Pin_1, Componente1.A3
  N30: R4.P$2, R6.Pin_1, Componente1.A1

custom parts:
  BMP280: Temperature Humidity Barometric presure Sensor, I2C
  RTC_DS1302_module: Arduino module DS1302 SPI Real Time Clock
  LCM1602 IIC: I2C-Module to use a 1602 or 2004 LCD on with the wire.h libory Serial LCD Modul
  Water Level Sensor: A water level sensor. This sensor operates at 3V to 5V. The Sig (signal) pin outputs an analogue signal that is in proportion to the amount of water in contact with the sensor.
